// Logisim project Lab 1 Part 1 Multiplexer Schematic.circ as structural Verilog: 1 circuit, main circuit main
module main (
);

  wire _7404_out, _7408_2_out, _7408_out, _7432_out, s_out, x_out, y_out;

  // Buffer x has open pins: in=open, out=x_out
  // Buffer s has open pins: in=open, out=s_out
  // Buffer y has open pins: in=open, out=y_out
  not _7404 (_7404_out, s_out);
  and _7408 (_7408_out, x_out, _7404_out);
  and _7408_2 (_7408_2_out, y_out, s_out);
  or _7432 (_7432_out, _7408_out, _7408_2_out);
  // Buffer f has open pins: in=_7432_out, out=open

  // Notes on the sheet:
  //   1
  //   2
  //   1
  //   2
  //   1
  //   2
  //   3
  //   3
  //   1
  //   3
  //   2
endmodule
