// Logisim project Lab 1 Part 1 Multiplexer With 7400s Chips.circ as structural Verilog: 1 circuit, main circuit main
module main (
);

  wire n7408_1_p1, n7408_1_p2, n7408_1_p3, n7408_1_p4, n7408_1_p5, n7408_1_p6, n7432_1_p1;

  // _7408 7408_1: pin names not known; wires that end beside it: n7408_1_p1, n7408_1_p2, n7408_1_p3, n7408_1_p4, n7408_1_p5, n7408_1_p6
  // Buffer y has open pins: in=open, out=n7408_1_p5
  // Buffer x has open pins: in=open, out=n7408_1_p2
  // Buffer s has open pins: in=open, out=n7408_1_p4
  // Buffer buffer_1 has open pins: in=n7432_1_p1, out=open
  // _7432 7432_1: pin names not known; wires that end beside it: n7432_1_p1, n7408_1_p6, n7408_1_p3
  // _7404 7404_1: pin names not known; wires that end beside it: n7408_1_p4, n7408_1_p1
endmodule
