// Logisim project Lab 1 Part 2 Schematic.circ as structural Verilog: 1 circuit, main circuit main
module main (
  input  in_1,
  input  in_2,
  input  in_3,
  input  in_4,
  output _3
);

  wire _7404_2_out, _7404_3_out, _7404_4_out, _7404_5_out, _7404_out, _7408_2_out, _7408_3_out, _7408_4_out,
       _7408_5_out, _7408_6_out, _7408_out, _7432_2_out, _7432_3_out, _7432_out, a_out, b_out, c_out, d_out;

  buf a (a_out, in_1);
  buf b (b_out, in_2);
  buf c (c_out, in_3);
  buf d (d_out, in_4);
  not _7404 (_7404_out, c_out);
  not _7404_2 (_7404_2_out, a_out);
  not _7404_3 (_7404_3_out, c_out);
  not _7404_4 (_7404_4_out, b_out);
  and _7408 (_7408_out, a_out, _7404_out);
  and _7408_2 (_7408_2_out, _7404_2_out, d_out);
  and _7408_3 (_7408_3_out, b_out, _7404_3_out);
  and _7408_4 (_7408_4_out, _7404_4_out, d_out);
  or _7432 (_7432_out, _7408_out, _7408_2_out);
  not _7404_5 (_7404_5_out, b_out);
  or _7432_2 (_7432_2_out, _7408_3_out, _7408_4_out);
  and _7408_5 (_7408_5_out, _7432_out, _7404_5_out);
  and _7408_6 (_7408_6_out, a_out, _7432_2_out);
  buf f (_3, _7432_3_out);
  or _7432_3 (_7432_3_out, _7408_5_out, _7408_6_out);

  // Notes on the sheet:
  //   2
  //   1
  //   2
  //   1
  //   2
  //   1
  //   2
  //   1
  //   1
  //   2
  //   1
  //   2
  //   1
  //   2
  //   1
  //   2
  //   3
  //   1
  //   2
  //   3
  //   1
  //   3
  //   1
  //   2
  //   3
  //   3
  //   1
  //   1
  //   2
  //   2
  //   1
  //   3
  //   2
  //   3
  //   1
  //   2
  //   3
endmodule
