// Logisim project Lab 1 Part 2 Simpler With 7400s Chips.circ as structural Verilog: 1 circuit, main circuit main
module main (
  input  in_1,
  input  in_2,
  input  in_3,
  input  in_4,
  output out_5
);

  wire a_out, b_out, c_out, d_out, n7404_1_p2, n7404_1_p4, n7404_1_p7, n7408_1_p3, n7432_1_p3;

  buf a (a_out, in_1);
  buf c (c_out, in_2);
  buf b (b_out, in_3);
  buf d (d_out, in_4);
  // _7404 7404_1: pin names not known; wires that end beside it: c_out, n7404_1_p2, b_out, n7404_1_p4, n7404_1_p4, d_out, n7404_1_p7
  // _7408 7408_1: pin names not known; wires that end beside it: n7404_1_p2, a_out, n7408_1_p3
  buf f (out_5, n7432_1_p3);
  // _7432 7432_1: pin names not known; wires that end beside it: n7408_1_p3, n7404_1_p7, n7432_1_p3
endmodule
