// Logisim project Lab 1 Part 2 Simplier Schematic.circ as structural Verilog: 1 circuit, main circuit main
module main (
  input  in_1,
  input  _1,
  input  _1_2,
  input  in_4,
  output _3
);

  wire _7404_2_out, _7404_out, _7408_2_out, _7408_out, _7432_out, a_out, b_out, c_out, d_out;

  buf a (a_out, in_1);
  buf c (c_out, _1);
  not _7404 (_7404_out, c_out);
  not _7404_2 (_7404_2_out, b_out);
  buf b (b_out, _1_2);
  buf d (d_out, in_4);
  and _7408 (_7408_out, a_out, _7404_out);
  and _7408_2 (_7408_2_out, _7404_2_out, d_out);
  or _7432 (_7432_out, _7408_out, _7408_2_out);
  buf f (_3, _7432_out);

  // Notes on the sheet:
  //   2
  //   2
  //   1
  //   3
  //   2
  //   1
  //   3
  //   2
  //   1
  //   2
endmodule
