// Logisim project D Flip-Flop.circ as structural Verilog: 1 circuit, main circuit main
module main (
  input  D,
  input  clk,
  output Q,
  output Q_tilde
);

  wire nand_1_out, nand_2_out, not_1_out;

  not not_1 (not_1_out, D);
  nand nand_1 (nand_1_out, D, clk);
  nand nand_2 (nand_2_out, clk, not_1_out);
  nand nand_3 (Q, nand_1_out, Q_tilde);
  nand nand_4 (Q_tilde, Q, nand_2_out);

  // Notes on the sheet:
  //   Q_tilde: pull=up
endmodule
